// Logisim project singleCycleCPUCompletedImplementingBlt.circ as structural Verilog: 4 circuits, main circuit register32
module register32 (
  input  [4:0] Write_Register_e227362b,
  input  [31:0] Write_Data_4f9e5b95,
  input  [4:0] Read_Address_1_49feeafd,
  input  [4:0] Read_Address_2_a255d371,
  input  Write_Enable_dc9b5f36,
  input  CLK,
  input  reset,
  output [31:0] Read_Data_1_98810816,
  output [31:0] Read_Data_2_6323e16b
);

  wire and_1_out, and_2_out, and_3_out, and_4_out, and_5_out, and_6_out, and_7_out, and_8_out, and_9_out,
       and_10_out, and_11_out, and_12_out, and_13_out, and_14_out, and_15_out, and_16_out, and_17_out,
       and_18_out, and_19_out, and_20_out, and_21_out, and_22_out, and_23_out, and_24_out, and_25_out,
       and_26_out, and_27_out, and_28_out, and_29_out, and_30_out, and_31_out, and_32_out, decoder_1_out0,
       decoder_1_out1, decoder_1_out2, decoder_1_out3, decoder_1_out4, decoder_1_out5, decoder_1_out6,
       decoder_1_out7, decoder_1_out8, decoder_1_out9, decoder_1_out10, decoder_1_out11, decoder_1_out12,
       decoder_1_out13, decoder_1_out14, decoder_1_out15, decoder_1_out16, decoder_1_out17, decoder_1_out18,
       decoder_1_out19, decoder_1_out20, decoder_1_out21, decoder_1_out22, decoder_1_out23, decoder_1_out24,
       decoder_1_out25, decoder_1_out26, decoder_1_out27, decoder_1_out28, decoder_1_out29, decoder_1_out30,
       decoder_1_out31;
  wire [31:0] register_1_q, register_2_q, register_3_q, register_4_q, register_5_q, register_6_q,
       register_7_q, register_8_q, register_9_q, register_10_q, register_11_q, register_12_q, register_13_q,
       register_14_q, register_15_q, register_16_q, register_17_q, register_18_q, register_19_q,
       register_20_q, register_21_q, register_22_q, register_23_q, register_24_q, register_25_q,
       register_26_q, register_27_q, register_28_q, register_29_q, register_30_q, register_31_q,
       register_32_q;

  Decoder #(.select(5)) decoder_1 (
    .out0(decoder_1_out0), .out1(decoder_1_out1), .out2(decoder_1_out2), .out3(decoder_1_out3),
    .out4(decoder_1_out4), .out5(decoder_1_out5), .out6(decoder_1_out6), .out7(decoder_1_out7),
    .out8(decoder_1_out8), .out9(decoder_1_out9), .out10(decoder_1_out10), .out11(decoder_1_out11),
    .out12(decoder_1_out12), .out13(decoder_1_out13), .out14(decoder_1_out14), .out15(decoder_1_out15),
    .out16(decoder_1_out16), .out17(decoder_1_out17), .out18(decoder_1_out18), .out19(decoder_1_out19),
    .out20(decoder_1_out20), .out21(decoder_1_out21), .out22(decoder_1_out22), .out23(decoder_1_out23),
    .out24(decoder_1_out24), .out25(decoder_1_out25), .out26(decoder_1_out26), .out27(decoder_1_out27),
    .out28(decoder_1_out28), .out29(decoder_1_out29), .out30(decoder_1_out30), .out31(decoder_1_out31),
    .sel(Write_Register_e227362b));  // open: en
  and and_1 (and_1_out, decoder_1_out0, Write_Enable_dc9b5f36);
  and and_2 (and_2_out, decoder_1_out1, Write_Enable_dc9b5f36);
  and and_3 (and_3_out, decoder_1_out2, Write_Enable_dc9b5f36);
  and and_4 (and_4_out, decoder_1_out3, Write_Enable_dc9b5f36);
  and and_5 (and_5_out, decoder_1_out4, Write_Enable_dc9b5f36);
  and and_6 (and_6_out, decoder_1_out5, Write_Enable_dc9b5f36);
  and and_7 (and_7_out, decoder_1_out6, Write_Enable_dc9b5f36);
  and and_8 (and_8_out, decoder_1_out7, Write_Enable_dc9b5f36);
  Register #(.width(32)) register_1 (.D(Write_Data_4f9e5b95), .en(and_1_out), .Q(register_1_q), .clk(CLK), .clr(1'b1));
  Register #(.width(32)) register_2 (.D(Write_Data_4f9e5b95), .en(and_2_out), .Q(register_2_q), .clk(CLK), .clr(reset));
  Register #(.width(32)) register_3 (.D(Write_Data_4f9e5b95), .en(and_3_out), .Q(register_3_q), .clk(CLK), .clr(reset));
  Register #(.width(32)) register_4 (.D(Write_Data_4f9e5b95), .en(and_4_out), .Q(register_4_q), .clk(CLK), .clr(reset));
  Register #(.width(32)) register_5 (.D(Write_Data_4f9e5b95), .en(and_5_out), .Q(register_5_q), .clk(CLK), .clr(reset));
  Register #(.width(32)) register_6 (.D(Write_Data_4f9e5b95), .en(and_6_out), .Q(register_6_q), .clk(CLK), .clr(reset));
  Register #(.width(32)) register_7 (.D(Write_Data_4f9e5b95), .en(and_7_out), .Q(register_7_q), .clk(CLK), .clr(reset));
  Register #(.width(32)) register_8 (.D(Write_Data_4f9e5b95), .en(and_8_out), .Q(register_8_q), .clk(CLK), .clr(reset));
  and and_9 (and_9_out, decoder_1_out8, Write_Enable_dc9b5f36);
  and and_10 (and_10_out, decoder_1_out9, Write_Enable_dc9b5f36);
  and and_11 (and_11_out, decoder_1_out10, Write_Enable_dc9b5f36);
  and and_12 (and_12_out, decoder_1_out11, Write_Enable_dc9b5f36);
  and and_13 (and_13_out, decoder_1_out12, Write_Enable_dc9b5f36);
  and and_14 (and_14_out, decoder_1_out13, Write_Enable_dc9b5f36);
  and and_15 (and_15_out, decoder_1_out14, Write_Enable_dc9b5f36);
  and and_16 (and_16_out, decoder_1_out15, Write_Enable_dc9b5f36);
  Register #(.width(32)) register_9 (.D(Write_Data_4f9e5b95), .en(and_9_out), .Q(register_9_q), .clk(CLK), .clr(reset));
  Register #(.width(32)) register_10 (
    .D(Write_Data_4f9e5b95), .en(and_10_out), .Q(register_10_q), .clk(CLK), .clr(reset));
  Register #(.width(32)) register_11 (
    .D(Write_Data_4f9e5b95), .en(and_11_out), .Q(register_11_q), .clk(CLK), .clr(reset));
  Register #(.width(32)) register_12 (
    .D(Write_Data_4f9e5b95), .en(and_12_out), .Q(register_12_q), .clk(CLK), .clr(reset));
  Register #(.width(32)) register_13 (
    .D(Write_Data_4f9e5b95), .en(and_13_out), .Q(register_13_q), .clk(CLK), .clr(reset));
  Register #(.width(32)) register_14 (
    .D(Write_Data_4f9e5b95), .en(and_14_out), .Q(register_14_q), .clk(CLK), .clr(reset));
  Register #(.width(32)) register_15 (
    .D(Write_Data_4f9e5b95), .en(and_15_out), .Q(register_15_q), .clk(CLK), .clr(reset));
  Register #(.width(32)) register_16 (
    .D(Write_Data_4f9e5b95), .en(and_16_out), .Q(register_16_q), .clk(CLK), .clr(reset));
  and and_17 (and_17_out, decoder_1_out16, Write_Enable_dc9b5f36);
  and and_18 (and_18_out, decoder_1_out17, Write_Enable_dc9b5f36);
  and and_19 (and_19_out, decoder_1_out18, Write_Enable_dc9b5f36);
  and and_20 (and_20_out, decoder_1_out19, Write_Enable_dc9b5f36);
  and and_21 (and_21_out, decoder_1_out20, Write_Enable_dc9b5f36);
  and and_22 (and_22_out, decoder_1_out21, Write_Enable_dc9b5f36);
  and and_23 (and_23_out, decoder_1_out22, Write_Enable_dc9b5f36);
  and and_24 (and_24_out, decoder_1_out23, Write_Enable_dc9b5f36);
  Register #(.width(32)) register_17 (
    .D(Write_Data_4f9e5b95), .en(and_17_out), .Q(register_17_q), .clk(CLK), .clr(reset));
  Register #(.width(32)) register_18 (
    .D(Write_Data_4f9e5b95), .en(and_18_out), .Q(register_18_q), .clk(CLK), .clr(reset));
  Register #(.width(32)) register_19 (
    .D(Write_Data_4f9e5b95), .en(and_19_out), .Q(register_19_q), .clk(CLK), .clr(reset));
  Register #(.width(32)) register_20 (
    .D(Write_Data_4f9e5b95), .en(and_20_out), .Q(register_20_q), .clk(CLK), .clr(reset));
  Register #(.width(32)) register_21 (
    .D(Write_Data_4f9e5b95), .en(and_21_out), .Q(register_21_q), .clk(CLK), .clr(reset));
  Register #(.width(32)) register_22 (
    .D(Write_Data_4f9e5b95), .en(and_22_out), .Q(register_22_q), .clk(CLK), .clr(reset));
  Register #(.width(32)) register_23 (
    .D(Write_Data_4f9e5b95), .en(and_23_out), .Q(register_23_q), .clk(CLK), .clr(reset));
  Register #(.width(32)) register_24 (
    .D(Write_Data_4f9e5b95), .en(and_24_out), .Q(register_24_q), .clk(CLK), .clr(reset));
  and and_25 (and_25_out, decoder_1_out24, Write_Enable_dc9b5f36);
  and and_26 (and_26_out, decoder_1_out25, Write_Enable_dc9b5f36);
  and and_27 (and_27_out, decoder_1_out26, Write_Enable_dc9b5f36);
  and and_28 (and_28_out, decoder_1_out27, Write_Enable_dc9b5f36);
  and and_29 (and_29_out, decoder_1_out28, Write_Enable_dc9b5f36);
  and and_30 (and_30_out, decoder_1_out29, Write_Enable_dc9b5f36);
  and and_31 (and_31_out, decoder_1_out30, Write_Enable_dc9b5f36);
  and and_32 (and_32_out, decoder_1_out31, Write_Enable_dc9b5f36);
  Register #(.width(32)) register_25 (
    .D(Write_Data_4f9e5b95), .en(and_25_out), .Q(register_25_q), .clk(CLK), .clr(reset));
  Register #(.width(32)) register_26 (
    .D(Write_Data_4f9e5b95), .en(and_26_out), .Q(register_26_q), .clk(CLK), .clr(reset));
  Register #(.width(32)) register_27 (
    .D(Write_Data_4f9e5b95), .en(and_27_out), .Q(register_27_q), .clk(CLK), .clr(reset));
  Register #(.width(32)) register_28 (
    .D(Write_Data_4f9e5b95), .en(and_28_out), .Q(register_28_q), .clk(CLK), .clr(reset));
  Register #(.width(32)) register_29 (
    .D(Write_Data_4f9e5b95), .en(and_29_out), .Q(register_29_q), .clk(CLK), .clr(reset));
  Register #(.width(32)) register_30 (
    .D(Write_Data_4f9e5b95), .en(and_30_out), .Q(register_30_q), .clk(CLK), .clr(reset));
  Register #(.width(32)) register_31 (
    .D(Write_Data_4f9e5b95), .en(and_31_out), .Q(register_31_q), .clk(CLK), .clr(reset));
  Register #(.width(32)) register_32 (
    .D(Write_Data_4f9e5b95), .en(and_32_out), .Q(register_32_q), .clk(CLK), .clr(reset));
  Multiplexer #(.enable("true"), .select(5), .width(32)) multiplexer_1 (
    .in0(register_1_q), .in1(register_2_q), .in2(register_3_q), .in3(register_4_q), .in4(register_5_q),
    .in5(register_6_q), .in6(register_7_q), .in7(register_8_q), .in8(register_9_q), .in9(register_10_q),
    .in10(register_11_q), .in11(register_12_q), .in12(register_13_q), .in13(register_14_q),
    .in14(register_15_q), .in15(register_16_q), .in16(register_17_q), .in17(register_18_q),
    .in18(register_19_q), .in19(register_20_q), .in20(register_21_q), .in21(register_22_q),
    .in22(register_23_q), .in23(register_24_q), .in24(register_25_q), .in25(register_26_q),
    .in26(register_27_q), .in27(register_28_q), .in28(register_29_q), .in29(register_30_q),
    .in30(register_31_q), .in31(register_32_q), .out(Read_Data_1_98810816), .sel(Read_Address_1_49feeafd));  // open: en
  Multiplexer #(.enable("true"), .select(5), .width(32)) multiplexer_2 (
    .in0(register_1_q), .in1(register_2_q), .in2(register_3_q), .in3(register_4_q), .in4(register_5_q),
    .in5(register_6_q), .in6(register_7_q), .in7(register_8_q), .in8(register_9_q), .in9(register_10_q),
    .in10(register_11_q), .in11(register_12_q), .in12(register_13_q), .in13(register_14_q),
    .in14(register_15_q), .in15(register_16_q), .in16(register_17_q), .in17(register_18_q),
    .in18(register_19_q), .in19(register_20_q), .in20(register_21_q), .in21(register_22_q),
    .in22(register_23_q), .in23(register_24_q), .in24(register_25_q), .in25(register_26_q),
    .in26(register_27_q), .in27(register_28_q), .in28(register_29_q), .in29(register_30_q),
    .in30(register_31_q), .in31(register_32_q), .out(Read_Data_2_6323e16b), .sel(Read_Address_2_a255d371));  // open: en

  // Notes on the sheet:
  //   Zero Register
endmodule

module nekitest (
  input  in_1,
  input  in_2,
  input  [31:0] for_test_input,
  input  [31:0] Data_to_Store,
  input  [1:0] in_5,
  output [1:0] ALU_opcode,
  output Branchh,
  output Result_Src,
  output Mem_Write,
  output ALU_Src,
  output [1:0] imm_src,
  output [2:0] out_12,
  output [31:0] out_13,
  output [31:0] out_14,
  output [4:0] out_15,
  output [31:0] out_16,
  output [23:0] out_17,
  output [31:0] out_18,
  output [31:0] out_19,
  output [31:0] readData2,
  output [31:0] readData3,
  output [31:0] out_22,
  output [31:0] out_23,
  output [1:0] out_24,
  output [23:0] out_25,
  output [31:0] Fetched_instruction,
  output Zero_Flag,
  output [2:0] out_28,
  output [31:0] Immediate_value,
  output [2:0] out_30,
  output [2:0] out_31,
  output [31:0] B_type_immediate,
  output [2:0] out_33,
  output [2:0] out_34,
  output [2:0] out_35,
  output [1:0] out_36,
  output [1:0] out_37,
  output [1:0] out_38
);

  wire and_2_out, CLK, comparator_1_eq, comparator_2_eq, comparator_3_eq, comparator_4_eq, comparator_5_eq,
       comparator_6_eq, comparator_7_eq, comparator_8_eq, comparator_9_eq, comparator_10_eq,
       comparator_11_eq, comparator_12_eq, comparator_13_eq, comparator_14_eq, comparator_15_eq,
       comparator_16_eq, comparator_17_lt, comparator_18_gt, xor_1_out;
  wire [1:0] multiplexer_12_out, multiplexer_13_out, multiplexer_14_out, multiplexer_15_out;
  wire [2:0] multiplexer_3_out, multiplexer_4_out, multiplexer_5_out, multiplexer_6_out, multiplexer_7_out,
       multiplexer_8_out, multiplexer_17_out, multiplexer_18_out, multiplexer_19_out, multiplexer_20_out;
  wire [8:8] multiplexer_21_out;
  wire [31:0] adder_3_out, and_1_out, bit_extender_1_out, bit_extender_2_out, bit_extender_4_out,
       bit_extender_5_out, multiplexer_1_out, subtractor_1_out;

  Adder #(.width(32)) adder_1 (.a(32'h4), .b(out_14), .out(out_16));  // open: cin, cout
  Adder #(.width(32)) adder_2 (.a(B_type_immediate), .b(out_14), .out(out_18));  // open: cin, cout
  Multiplexer #(.width(32)) multiplexer_1 (.in0(out_16), .in1(out_18), .out(multiplexer_1_out), .sel(and_2_out));
  Register #(.width(32)) register_1 (.D(multiplexer_1_out), .Q(out_14), .clk(CLK), .clr(in_2));  // open: en
  Clock clock_1 (.out(CLK));
  ROM #(.addrWidth(24), .dataWidth(32)) rom_1 (.addr(out_14[25:2]), .data(Fetched_instruction));
  register32 register32_1 (
    .reset(in_2), .Write_Data_4f9e5b95(out_13), .Read_Address_1_49feeafd(Fetched_instruction[19:15]),
    .Read_Address_2_a255d371(Fetched_instruction[24:20]),
    .Write_Register_e227362b(Fetched_instruction[11:7]), .Write_Enable_dc9b5f36(multiplexer_21_out[8]),
    .CLK(CLK), .Read_Data_2_6323e16b(out_19), .Read_Data_1_98810816(readData3));
  assign bit_extender_1_out = {{20{1'b0}}, Fetched_instruction[31:20]};  // Bit_Extender bit_extender_1
  assign bit_extender_2_out = {{20{1'b0}}, {Fetched_instruction[31:25], Fetched_instruction[11:7]}};  // Bit_Extender bit_extender_2
  assign B_type_immediate = {{19{Fetched_instruction[31]}}, {Fetched_instruction[31], Fetched_instruction[7], Fetched_instruction[30:25], Fetched_instruction[11:8], 1'b0}};  // Bit_Extender bit_extender_3
  Multiplexer #(.select(2), .width(32)) multiplexer_2 (
    .in0(bit_extender_1_out), .in1(bit_extender_2_out), .in2(B_type_immediate), .out(Immediate_value),
    .sel(imm_src));  // open: in3
  Multiplexer #(.width(3)) multiplexer_3 (.in0(3'b000), .in1(3'b001), .out(multiplexer_3_out), .sel(comparator_1_eq));
  Comparator #(.width(7)) comparator_1 (
    .a(Fetched_instruction[6:0]), .b(7'b0000011), .eq(comparator_1_eq));  // open: gt, lt
  Multiplexer #(.width(3)) multiplexer_4 (.in0(3'b000), .in1(3'b010), .out(multiplexer_4_out), .sel(comparator_2_eq));
  Comparator #(.width(7)) comparator_2 (
    .a(Fetched_instruction[6:0]), .b(7'b0100011), .eq(comparator_2_eq));  // open: gt, lt
  Multiplexer #(.width(3)) multiplexer_5 (.in0(3'b000), .in1(3'b011), .out(multiplexer_5_out), .sel(comparator_3_eq));
  Comparator #(.width(7)) comparator_3 (
    .a(Fetched_instruction[6:0]), .b(7'b0110011), .eq(comparator_3_eq));  // open: gt, lt
  Multiplexer #(.width(3)) multiplexer_6 (.in0(3'b000), .in1(3'b100), .out(multiplexer_6_out), .sel(comparator_4_eq));
  Comparator #(.width(7)) comparator_4 (
    .a(Fetched_instruction[6:0]), .b(7'b1100011), .eq(comparator_4_eq));  // open: gt, lt
  Multiplexer #(.width(3)) multiplexer_7 (.in0(3'b000), .in1(3'b101), .out(multiplexer_7_out), .sel(comparator_5_eq));
  Comparator #(.width(7)) comparator_5 (
    .a(Fetched_instruction[6:0]), .b(7'b0010011), .eq(comparator_5_eq));  // open: gt, lt
  Multiplexer #(.width(3)) multiplexer_8 (.in0(3'b000), .in1(3'b110), .out(multiplexer_8_out), .sel(comparator_6_eq));
  Comparator #(.width(7)) comparator_6 (
    .a(Fetched_instruction[6:0]), .b(7'b1100011), .eq(comparator_6_eq));  // open: gt, lt
  Multiplexer #(.width(32)) multiplexer_9 (.in0(out_19), .in1(Immediate_value), .out(readData2), .sel(ALU_Src));
  Comparator #(.width(2)) comparator_7 (
    .a({Fetched_instruction[30], Fetched_instruction[5]}), .b(2'b11), .eq(comparator_7_eq));  // open: gt, lt
  Multiplexer #(.width(3)) multiplexer_10 (.in0(3'b000), .in1(3'b001), .out(out_30), .sel(comparator_7_eq));
  Comparator #(.width(3)) comparator_8 (
    .a(Fetched_instruction[14:12]), .b(3'b000), .eq(comparator_8_eq));  // open: gt, lt
  Comparator #(.width(3)) comparator_9 (
    .a(Fetched_instruction[14:12]), .b(3'b010), .eq(comparator_9_eq));  // open: gt, lt
  Comparator #(.width(3)) comparator_10 (
    .a(Fetched_instruction[14:12]), .b(3'b100), .eq(comparator_10_eq));  // open: gt, lt
  Comparator #(.width(3)) comparator_11 (
    .a(Fetched_instruction[14:12]), .b(3'b110), .eq(comparator_11_eq));  // open: gt, lt
  Comparator #(.width(3)) comparator_12 (
    .a(Fetched_instruction[14:12]), .b(3'b111), .eq(comparator_12_eq));  // open: gt, lt
  Comparator #(.width(2)) comparator_13 (.a(ALU_opcode), .b(2'b00), .eq(comparator_13_eq));  // open: gt, lt
  Comparator #(.width(2)) comparator_14 (.a(ALU_opcode), .b(2'b01), .eq(comparator_14_eq));  // open: gt, lt
  Comparator #(.width(2)) comparator_15 (.a(ALU_opcode), .b(2'b10), .eq(comparator_15_eq));  // open: gt, lt
  Comparator #(.width(2)) comparator_16 (.a(ALU_opcode), .b(2'b11), .eq(comparator_16_eq));  // open: gt, lt
  Multiplexer #(.width(2)) multiplexer_11 (.in0(2'b00), .in1(in_5), .out(out_38), .sel(xor_1_out));
  xor xor_1 (xor_1_out, in_5[0], in_5[1]);
  assign out_12 = multiplexer_3_out | multiplexer_4_out | multiplexer_5_out | multiplexer_6_out | multiplexer_7_out | multiplexer_8_out;  // OR_Gate or_1, 3 bits wide
  Multiplexer #(.width(2)) multiplexer_12 (.in0(2'b00), .in1(2'b00), .out(multiplexer_12_out), .sel(comparator_13_eq));
  Multiplexer #(.width(2)) multiplexer_13 (.in0(2'b00), .in1(2'b01), .out(multiplexer_13_out), .sel(comparator_14_eq));
  Multiplexer #(.width(2)) multiplexer_14 (.in0(2'b00), .in1(2'b10), .out(multiplexer_14_out), .sel(comparator_15_eq));
  Multiplexer #(.width(2)) multiplexer_15 (.in0(2'b00), .in1(2'b10), .out(multiplexer_15_out), .sel(comparator_16_eq));
  Multiplexer #(.width(3)) multiplexer_16 (.in0(3'b000), .in1(out_30), .out(out_31), .sel(comparator_8_eq));
  Multiplexer #(.width(3)) multiplexer_17 (.in0(3'b000), .in1(3'b101), .out(multiplexer_17_out), .sel(comparator_9_eq));
  Multiplexer #(.width(3)) multiplexer_18 (
    .in0(3'b000), .in1(3'b110), .out(multiplexer_18_out), .sel(comparator_10_eq));
  Multiplexer #(.width(3)) multiplexer_19 (
    .in0(3'b000), .in1(3'b011), .out(multiplexer_19_out), .sel(comparator_11_eq));
  Multiplexer #(.width(3)) multiplexer_20 (
    .in0(3'b000), .in1(3'b010), .out(multiplexer_20_out), .sel(comparator_12_eq));
  Multiplexer #(.select(3), .width(9)) multiplexer_21 (
    .in0({9{1'b0}}), .in1(9'h129), .in2(9'h70), .in3(9'h102), .in4(9'h95), .in5(9'h120), .in6(9'h97),
    .in7({9{1'b0}}),
    .out({multiplexer_21_out[8], imm_src, ALU_Src, Mem_Write, Result_Src, Branchh, ALU_opcode}), .sel(out_12));
  assign out_36 = multiplexer_12_out | multiplexer_13_out | multiplexer_14_out | multiplexer_15_out;  // OR_Gate or_2, 2 bits wide
  assign out_34 = out_31 | multiplexer_17_out | multiplexer_18_out | multiplexer_19_out | multiplexer_20_out;  // OR_Gate or_3, 3 bits wide
  Multiplexer #(.select(2), .width(3)) multiplexer_22 (
    .in0(3'b000), .in1(3'b001), .in2(out_34), .out(out_28), .sel(out_36));  // open: in3
  Multiplexer #(.width(32)) multiplexer_23 (.in0(out_23), .in1(out_22), .out(out_13), .sel(Result_Src));
  Adder #(.width(32)) adder_3 (.a(readData3), .b(readData2), .out(adder_3_out));  // open: cin, cout
  Subtractor #(.width(32)) subtractor_1 (.a(readData3), .b(readData2), .out(subtractor_1_out));  // open: bin, bout
  assign and_1_out = readData3 & readData2;  // AND_Gate and_1, 32 bits wide
  Comparator #(.width(32)) comparator_17 (.a(readData3), .b(readData2), .lt(comparator_17_lt));  // open: gt, eq
  Comparator #(.width(32)) comparator_18 (.a(readData3), .b(readData2), .gt(comparator_18_gt));  // open: eq, lt
  assign bit_extender_4_out = {{31{comparator_17_lt}}, comparator_17_lt};  // Bit_Extender bit_extender_4
  assign bit_extender_5_out = {{31{comparator_18_gt}}, comparator_18_gt};  // Bit_Extender bit_extender_5
  Multiplexer #(.select(3), .width(32)) multiplexer_24 (
    .in0(adder_3_out), .in1(subtractor_1_out), .in2(and_1_out), .in5(bit_extender_4_out),
    .in6(bit_extender_5_out), .out(out_23), .sel(out_28));  // open: in3, in4, in7
  and and_2 (and_2_out, Branchh, Zero_Flag);
  Comparator #(.width(32)) comparator_19 (.a(out_23), .b({32{1'b0}}), .eq(Zero_Flag));  // open: gt, lt
  RAM #(.addrWidth(24), .dataWidth(32), .enables("line")) ram_1 (
    .addr(out_23[23:0]), .we(Mem_Write), .clk(CLK), .din(out_19), .dout(out_22));

  assign out_15 = Fetched_instruction[11:7];
  assign out_17 = out_14[25:2];
  assign out_24 = imm_src;
  assign out_25 = out_23[23:0];
  assign out_33 = out_28;
  assign out_35 = Fetched_instruction[14:12];
  assign out_37 = ALU_opcode;

  // Other names for the same wires on the sheet: RES = in_2

  // Notes on the sheet:
  //   contents of rom_1 (hex, n*v repeats v):
  //   293 800313 393 100413 8383b3 838433 128293 fe62cae3 8004b3
  //   lw => 0000011
  //   sw => 0100011
  //   r-type => 0110011
  //   beq => 1100011
  //   addi => 0010011
  //   blt => 1100011
  //   op
  //   func7
  //   fun3
  //   ALUop
  //   reg write
  //   ALU Control Singal Input
  //   ALU Result
endmodule

module main (
);

  wire comparator_1_eq, comparator_2_eq, comparator_3_eq, comparator_4_eq, comparator_5_eq, comparator_6_eq,
       comparator_7_eq, comparator_8_eq;
  wire [1:0] undriven_2, undriven_6;
  wire [2:0] multiplexer_1_out, multiplexer_2_out, multiplexer_3_out, multiplexer_4_out, multiplexer_5_out,
       multiplexer_6_out, multiplexer_7_out, multiplexer_8_out, multiplexer_9_out, or_1_out, or_2_out,
       undriven, undriven_5;
  wire [5:5] undriven_3, undriven_4;

  Comparator #(.width(2)) comparator_1 (
    .a({undriven_4[5], undriven_3[5]}), .b(2'b11), .eq(comparator_1_eq));  // open: gt, lt
  Multiplexer #(.width(3)) multiplexer_1 (.in0(3'b000), .in1(3'b001), .out(multiplexer_1_out), .sel(comparator_1_eq));
  Comparator #(.width(3)) comparator_2 (.a(undriven_5), .b(3'b000), .eq(comparator_2_eq));  // open: gt, lt
  Comparator #(.width(3)) comparator_3 (
    .a(undriven_5), .b(3'b010), .eq(comparator_3_eq), .lt(comparator_3_eq));  // open: gt
  Comparator #(.width(3)) comparator_4 (.a(undriven), .b(3'b110), .eq(comparator_4_eq));  // open: gt, lt
  Comparator #(.width(3)) comparator_5 (.a(undriven_5), .b(3'b111), .eq(comparator_5_eq));  // open: gt, lt
  Comparator #(.width(2)) comparator_6 (.a(undriven_6), .b(2'b00), .eq(comparator_6_eq));  // open: gt, lt
  Comparator #(.width(2)) comparator_7 (.a(undriven_2), .b(2'b01), .eq(comparator_7_eq));  // open: gt, lt
  Comparator #(.width(2)) comparator_8 (.a(undriven_6), .b(2'b10), .eq(comparator_8_eq));  // open: gt, lt
  Multiplexer #(.width(3)) multiplexer_2 (.in0(3'b000), .in1(3'b000), .out(multiplexer_2_out), .sel(comparator_6_eq));
  Multiplexer #(.width(3)) multiplexer_3 (.in0(3'b000), .in1(3'b001), .out(multiplexer_3_out), .sel(comparator_7_eq));
  Multiplexer #(.width(3)) multiplexer_4 (.in0(3'b000), .in1(3'b010), .out(multiplexer_4_out), .sel(comparator_8_eq));
  Multiplexer #(.width(3)) multiplexer_5 (
    .in0(3'b000), .in1(multiplexer_1_out), .out(multiplexer_5_out), .sel(comparator_2_eq));
  Multiplexer #(.width(3)) multiplexer_6 (.in0(3'b000), .in1(3'b101), .out(multiplexer_6_out), .sel(comparator_3_eq));
  Multiplexer #(.width(3)) multiplexer_7 (.in0(3'b000), .in1(3'b011), .out(multiplexer_7_out), .sel(comparator_4_eq));
  Multiplexer #(.width(3)) multiplexer_8 (.in0(3'b000), .in1(3'b010), .out(multiplexer_8_out), .sel(comparator_5_eq));
  assign or_1_out = multiplexer_2_out | multiplexer_3_out | multiplexer_4_out;  // OR_Gate or_1, 3 bits wide
  assign or_2_out = multiplexer_5_out | multiplexer_6_out | multiplexer_7_out | multiplexer_8_out;  // OR_Gate or_2, 3 bits wide
  Multiplexer #(.select(3), .width(3)) multiplexer_9 (
    .in0(3'b000), .in1(3'b111), .in2(or_2_out), .out(multiplexer_9_out), .sel(or_1_out));  // open: in3, in4, in5, in6, in7

  // Notes on the sheet:
  //   op
  //   func7
  //   not sure what should be the input here !!!
  //   fun3
  //   ALUop
endmodule

module disc (
  input  P,
  input  Q,
  input  R,
  input  S,
  output out_5
);

  wire and_1_out, and_2_out, not_1_out, not_2_out, not_3_out, or_1_out, or_2_out, or_3_out, xnor_1_out,
       xor_1_out;

  or or_1 (or_1_out, R, P);
  and and_1 (and_1_out, P, Q);
  xor xor_1 (xor_1_out, Q, R);
  not not_1 (not_1_out, and_1_out);
  not not_2 (not_2_out, R);
  or or_2 (or_2_out, not_1_out, not_2_out);
  xnor xnor_1 (xnor_1_out, or_2_out, xor_1_out);
  or or_3 (or_3_out, xnor_1_out, R);
  and and_2 (and_2_out, or_1_out, or_3_out);
  not not_3 (not_3_out, and_2_out);
  or or_4 (out_5, not_3_out, S);
endmodule
